# Fritzing sketch AR13 (saved by Fritzing 0.9.3b)

parts:
  Mod1 = Arduino Sensor Shield v5.0
  J1 = Piezo Speaker  # not connected
  M1 = fc-51 [package=THT]
  J2 = Basic Servo  # not connected
  LCD1 = LCD screen  # not connected
  LED1 = RGB LED (com. cathode, rbg) [package="5 mm [THT]"]  # not connected
  부품1 = Bluetooth HM-10

nets:
  N1: Mod1.A4-VCC, Mod1.10-V, Mod1.4-V, Mod1.ParallelLCD-VCC, M1.pin3, 부품1.VCC
  N2: Mod1.A4-GND, Mod1.10-G, Mod1.4-G, Mod1.ParallelLCD-GND, M1.pin2, 부품1.GND
  N3: Mod1.10-S, Mod1.ParallelLCD-D10, M1.pin1
  N4: Mod1.5-S, Mod1.ParallelLCD-D5, 부품1.RXD
  N5: Mod1.4-S, Mod1.ParallelLCD-D4, 부품1.TXD

custom parts:
  Arduino Sensor Shield v5.0: Arduino Sensor Shield v5.0 provides I2C interface, Bluetooth module communication interface, SD card module communication interface, APC220 wireless RF modules communication interface, RB URF V1.1 ultrasonic sensors interface, 12864 LCD serial and parallel interface, 32 servo controller interfaces. In addition (with the sel jumper removed) allows an external power supply for the servos as the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
